// Logisim project CLA.circ as structural Verilog: 6 circuits, main circuit main
module main (
  input  in_1,
  input  in_2,
  input  in_3,
  input  in_4,
  input  in_5,
  input  in_6,
  input  in_7,
  input  in_8,
  input  in_9,
  input  in_10,
  input  in_11,
  input  in_12,
  input  in_13,
  input  in_14,
  input  in_15,
  input  in_16,
  input  Uszkodzone,
  input  in_18,
  input  Uszkodzone_2,
  input  in_20,
  input  in_21,
  input  in_22,
  input  in_23,
  input  in_24,
  input  in_25,
  input  in_26,
  input  in_27,
  input  in_28,
  input  in_29,
  input  in_30,
  input  in_31,
  input  in_32,
  input  in_33,
  input  in_34,
  input  in_35,
  input  in_36,
  input  Uszkodzone_3,
  input  in_38,
  input  in_39,
  input  in_40,
  input  Uszkodzone_4,
  input  Uszkodzone_5,
  input  Uszkodzone_6,
  input  in_44,
  input  in_45,
  input  in_46,
  input  in_47,
  input  in_48,
  input  in_49,
  input  in_50,
  input  in_51,
  input  in_52,
  input  in_53,
  input  in_54,
  input  in_55,
  input  in_56,
  input  in_57,
  input  in_58,
  input  in_59,
  input  Uszkodzone_7,
  input  in_61,
  input  Uszkodzone_8,
  input  in_63,
  input  in_64,
  input  in_65,
  input  in_66,
  input  Uszkodzone_9,
  input  Uszkodzone_10,
  input  Uszkodzone_11,
  input  Uszkodzone_12,
  output out_71,
  output out_72,
  output out_73,
  output out_74,
  output out_75,
  output out_76,
  output out_77,
  output out_78,
  output out_79,
  output out_80,
  output out_81,
  output out_82,
  output out_83,
  output out_84,
  output out_85
);

  wire and_1_out, and_2_out, and_3_out, and_4_out, and_5_out, and_6_out, and_7_out, and_8_out, and_9_out,
       and_10_out, and_11_out, and_12_out, and_13_out, and_14_out, and_15_out, and_16_out, and_17_out,
       and_18_out, and_19_out, and_20_out, and_21_out, and_22_out, and_23_out, and_24_out, and_25_out,
       and_26_out, and_27_out, and_28_out, and_29_out, and_30_out, and_31_out, and_32_out, or_1_out,
       or_2_out, or_3_out, or_4_out, or_5_out, or_6_out, or_7_out, or_8_out, or_9_out, xor_1_out, xor_2_out,
       xor_3_out, xor_4_out, xor_5_out, xor_6_out, xor_7_out, xor_8_out, xor_9_out, xor_10_out, xor_11_out,
       xor_12_out, xor_13_out, xor_14_out, xor_15_out, xor_16_out, xor_17_out, xor_18_out, xor_19_out,
       xor_20_out, xor_21_out, xor_22_out, xor_23_out, xor_24_out, xor_25_out, xor_26_out, xor_27_out,
       xor_28_out, xor_29_out, xor_31_out, xor_32_out, xor_33_out, xor_34_out, xor_35_out, xor_38_out,
       xor_40_out, xor_43_out, xor_45_out, xor_49_out, xor_50_out, xor_51_out, xor_52_out, xor_53_out,
       xor_54_out, xor_55_out, xor_56_out, xor_57_out, xor_58_out, xor_59_out, xor_60_out, xor_61_out,
       xor_62_out, xor_63_out, xor_64_out, xor_65_out, xor_66_out, xor_67_out, xor_68_out;

  xor xor_1 (xor_1_out, in_29, in_23);
  and and_1 (and_1_out, in_29, in_23);
  xor xor_2 (xor_2_out, in_28, in_22);
  and and_2 (and_2_out, in_28, in_22);
  xor xor_3 (xor_3_out, in_27, in_21);
  and and_3 (and_3_out, in_27, in_21);
  xor xor_4 (xor_4_out, in_26, in_24);
  and and_4 (and_4_out, in_26, in_24);
  xor xor_5 (xor_5_out, in_35, in_34);
  and and_5 (and_5_out, in_35, in_34);
  xor xor_6 (xor_6_out, in_40, in_33);
  and and_6 (and_6_out, in_40, in_33);
  xor xor_7 (xor_7_out, in_39, in_32);
  and and_7 (and_7_out, in_39, in_32);
  xor xor_8 (xor_8_out, in_38, in_31);
  and and_8 (and_8_out, in_38, in_31);
  xor xor_9 (xor_9_out, in_3, xor_1_out);
  xor xor_10 (xor_10_out, in_4, and_1_out);
  xor xor_11 (xor_11_out, in_8, xor_2_out);
  xor xor_12 (xor_12_out, in_9, and_2_out);
  xor xor_13 (xor_13_out, in_14, xor_3_out);
  xor xor_14 (xor_14_out, in_15, and_3_out);
  xor xor_15 (xor_15_out, in_25, xor_4_out);
  xor xor_16 (xor_16_out, in_36, and_4_out);
  xor xor_17 (xor_17_out, in_46, xor_5_out);
  xor xor_18 (xor_18_out, in_47, and_5_out);
  xor xor_19 (xor_19_out, in_51, xor_6_out);
  xor xor_20 (xor_20_out, in_52, and_6_out);
  xor xor_21 (xor_21_out, in_57, xor_7_out);
  xor xor_22 (xor_22_out, in_58, and_7_out);
  xor xor_23 (xor_23_out, in_64, xor_8_out);
  xor xor_24 (xor_24_out, in_66, and_8_out);
  xor xor_25 (xor_25_out, in_1, xor_9_out);
  xor xor_26 (xor_26_out, xor_38_out, xor_11_out);
  xor xor_27 (xor_27_out, xor_40_out, xor_13_out);
  xor xor_28 (xor_28_out, or_3_out, Uszkodzone);
  xor xor_29 (xor_29_out, xor_28_out, xor_15_out);
  xor xor_30 (out_73, or_4_out, Uszkodzone_3);
  xor xor_31 (xor_31_out, in_44, xor_17_out);
  xor xor_32 (xor_32_out, xor_43_out, xor_19_out);
  xor xor_33 (xor_33_out, xor_45_out, xor_21_out);
  xor xor_34 (xor_34_out, or_7_out, Uszkodzone_7);
  xor xor_35 (xor_35_out, xor_34_out, xor_23_out);
  xor xor_36 (out_81, or_8_out, Uszkodzone_9);
  xor xor_37 (out_72, in_2, xor_25_out);
  xor xor_38 (xor_38_out, or_1_out, in_5);
  xor xor_39 (out_71, in_7, xor_26_out);
  xor xor_40 (xor_40_out, or_2_out, in_10);
  xor xor_41 (out_74, in_20, xor_29_out);
  xor xor_42 (out_80, in_45, xor_31_out);
  xor xor_43 (xor_43_out, or_5_out, in_48);
  xor xor_44 (out_79, in_50, xor_32_out);
  xor xor_45 (xor_45_out, or_6_out, in_53);
  xor xor_46 (out_82, in_63, xor_35_out);
  or or_1 (or_1_out, xor_10_out, xor_63_out);
  or or_2 (or_2_out, xor_12_out, xor_64_out, xor_65_out);
  xor xor_47 (out_75, in_12, xor_27_out);
  or or_3 (or_3_out, xor_14_out, xor_49_out, xor_50_out, xor_51_out);
  or or_4 (or_4_out, xor_16_out, xor_52_out, xor_53_out, xor_54_out, xor_55_out);
  or or_5 (or_5_out, xor_18_out, xor_66_out);
  or or_6 (or_6_out, xor_20_out, xor_67_out, xor_68_out);
  xor xor_48 (out_83, in_55, xor_33_out);
  or or_7 (or_7_out, xor_22_out, xor_56_out, xor_57_out, xor_58_out);
  or or_8 (or_8_out, xor_24_out, xor_59_out, xor_60_out, xor_61_out, xor_62_out);
  xor xor_49 (xor_49_out, and_9_out, in_16);
  xor xor_50 (xor_50_out, and_10_out, in_18);
  xor xor_51 (xor_51_out, and_11_out, Uszkodzone_2);
  xor xor_52 (xor_52_out, and_12_out, in_30);
  xor xor_53 (xor_53_out, and_13_out, Uszkodzone_4);
  xor xor_54 (xor_54_out, and_14_out, Uszkodzone_5);
  xor xor_55 (xor_55_out, and_15_out, Uszkodzone_6);
  xor xor_56 (xor_56_out, and_16_out, in_59);
  xor xor_57 (xor_57_out, and_17_out, in_61);
  xor xor_58 (xor_58_out, and_18_out, Uszkodzone_8);
  xor xor_59 (xor_59_out, and_19_out, in_65);
  xor xor_60 (xor_60_out, and_20_out, Uszkodzone_10);
  xor xor_61 (xor_61_out, and_21_out, Uszkodzone_11);
  xor xor_62 (xor_62_out, and_22_out, Uszkodzone_12);
  xor xor_63 (xor_63_out, and_23_out, in_6);
  xor xor_64 (xor_64_out, and_24_out, in_11);
  xor xor_65 (xor_65_out, and_25_out, in_13);
  and and_9 (and_9_out, xor_13_out, xor_12_out);
  and and_10 (and_10_out, xor_13_out, xor_11_out, xor_10_out);
  and and_11 (and_11_out, xor_13_out, xor_11_out, xor_9_out, in_1);
  and and_12 (and_12_out, xor_15_out, xor_14_out);
  and and_13 (and_13_out, xor_15_out, xor_13_out, xor_12_out);
  and and_14 (and_14_out, xor_15_out, xor_13_out, xor_11_out, xor_10_out);
  and and_15 (and_15_out, xor_15_out, xor_13_out, xor_11_out, xor_9_out, in_1);
  xor xor_66 (xor_66_out, and_26_out, in_49);
  xor xor_67 (xor_67_out, and_27_out, in_54);
  xor xor_68 (xor_68_out, and_28_out, in_56);
  and and_16 (and_16_out, xor_21_out, xor_20_out);
  and and_17 (and_17_out, xor_21_out, xor_19_out, xor_18_out);
  and and_18 (and_18_out, xor_21_out, xor_19_out, xor_17_out, in_44);
  and and_19 (and_19_out, xor_23_out, xor_22_out);
  and and_20 (and_20_out, xor_23_out, xor_21_out, xor_20_out);
  and and_21 (and_21_out, xor_23_out, xor_21_out, xor_19_out, xor_18_out);
  and and_22 (and_22_out, xor_23_out, xor_21_out, xor_19_out, xor_17_out, in_44);
  and and_23 (and_23_out, in_1, xor_9_out);
  and and_24 (and_24_out, xor_11_out, xor_10_out);
  and and_25 (and_25_out, xor_11_out, xor_9_out, in_1);
  and and_26 (and_26_out, in_44, xor_17_out);
  and and_27 (and_27_out, xor_19_out, xor_18_out);
  and and_28 (and_28_out, xor_19_out, xor_17_out, in_44);
  generatorResztowy generatorresztowy_1 (
    .X1(out_71), .X2(out_75), .X4(out_73), .X0(out_72), .X3(out_74), .Cout(out_76), .S(out_77));
  generatorResztowy generatorresztowy_2 (
    .X1(out_79), .X2(out_83), .X4(out_81), .X0(out_80), .X3(out_82), .Cout(out_84), .S(out_85));
  and and_29 (and_29_out, ~out_85, ~out_84, ~out_77, ~out_76);  // AND_Gate
  and and_30 (and_30_out, ~out_76, out_77, ~out_84, out_85);  // AND_Gate
  and and_31 (and_31_out, out_76, out_77, out_84, out_85);
  and and_32 (and_32_out, out_76, ~out_77, out_84, ~out_85);  // AND_Gate
  or or_9 (or_9_out, and_29_out, and_30_out, and_31_out, and_32_out);
  not not_1 (out_78, or_9_out);

  // Notes on the sheet:
  //   Uszkodzone
  //   Uszkodzone
  //   Uszkodzone
  //   Uszkodzone
  //   Uszkodzone
  //   Uszkodzone
  //   Uszkodzone
  //   Uszkodzone
  //   Uszkodzone
  //   Uszkodzone
  //   Uszkodzone
  //   Uszkodzone
  //   Uszkodzone
  //   Uszkodzone
  //   Uszkodzone
  //   Uszkodzone
  //   Uszkodzone
  //   Uszkodzone
  //   Uszkodzone
  //   Uszkodzone
  //   Uszkodzone
  //   Uszkodzone
  //   Uszkodzone
  //   Uszkodzone
  //   Uszkodzone
  //   Uszkodzone
  //   Uszkodzone
  //   Uszkodzone
  //   Uszkodzone
  //   Uszkodzone
  //   Uszkodzone
  //   Uszkodzone
  //   Uszkodzone
  //   Uszkodzone
  //   Uszkodzone
  //   Uszkodzone
  //   Uszkodzone
  //   Uszkodzone
  //   Uszkodzone
  //   Uszkodzone
endmodule

module FA101 (
  input  X1,
  input  Y1,
  input  Cin,
  output Cout,
  output S
);

  wire and_1_out, and_2_out, not_1_out, not_2_out, xor_1_out;

  not not_1 (not_1_out, X1);
  not not_2 (not_2_out, Cin);
  and and_1 (and_1_out, not_1_out, Y1);
  xor xor_1 (xor_1_out, not_1_out, Y1);
  or or_1 (Cout, and_1_out, and_2_out);
  and and_2 (and_2_out, xor_1_out, not_2_out);
  xor xor_2 (S, xor_1_out, not_2_out);
endmodule

module FA010 (
  input  X1,
  input  Y1,
  input  Cin,
  output Cout,
  output S
);

  wire and_1_out, and_2_out, not_1_out, xor_1_out;

  not not_1 (not_1_out, Y1);
  and and_1 (and_1_out, X1, not_1_out);
  xor xor_1 (xor_1_out, X1, not_1_out);
  or or_1 (Cout, and_1_out, and_2_out);
  and and_2 (and_2_out, xor_1_out, Cin);
  xor xor_2 (S, xor_1_out, Cin);
endmodule

module FA111 (
  input  X1,
  input  Y1,
  input  Cin,
  output Cout,
  output S
);

  wire and_1_out, and_2_out, not_1_out, not_2_out, not_3_out, xor_1_out;

  not not_1 (not_1_out, X1);
  not not_2 (not_2_out, Y1);
  not not_3 (not_3_out, Cin);
  and and_1 (and_1_out, not_1_out, not_2_out);
  xor xor_1 (xor_1_out, not_1_out, not_2_out);
  or or_1 (Cout, and_1_out, and_2_out);
  and and_2 (and_2_out, xor_1_out, not_3_out);
  xor xor_2 (S, xor_1_out, not_3_out);
endmodule

module FA110 (
  input  X1,
  input  Y1,
  input  Cin,
  output Cout,
  output S
);

  wire and_1_out, and_2_out, not_1_out, not_2_out, xor_1_out;

  not not_1 (not_1_out, Y1);
  not not_2 (not_2_out, Cin);
  and and_1 (and_1_out, X1, not_1_out);
  xor xor_1 (xor_1_out, X1, not_1_out);
  or or_1 (Cout, and_1_out, and_2_out);
  and and_2 (and_2_out, xor_1_out, not_2_out);
  xor xor_2 (S, xor_1_out, not_2_out);
endmodule

module generatorResztowy (
  input  X1,
  input  X2,
  input  X4,
  input  X0,
  input  X3,
  output Cout,
  output S
);

  wire fa010_1_cout, fa010_1_s, fa010_2_cout, fa010_2_s, fa010_3_cout, fa010_3_s, fa010_4_cout, fa010_4_s,
       fa010_5_cout, fa010_5_s, fa010_6_cout, fa010_6_s, fa010_7_cout, fa010_7_s, fa010_8_cout, fa010_8_s,
       fa101_1_cout, fa101_1_s, fa101_2_cout, fa101_2_s, fa101_3_cout, fa101_3_s, fa101_4_cout, fa101_4_s,
       fa111_1_cout, fa111_1_s;

  FA010 fa010_1 (.Cout(fa010_1_cout), .S(fa010_1_s));  // open: X1, Y1, Cin
  FA101 fa101_1 (.Cout(fa101_1_cout), .S(fa101_1_s));  // open: X1, Y1, Cin
  FA010 fa010_2 (.Cout(fa010_2_cout), .S(fa010_2_s));  // open: X1, Y1, Cin
  FA010 fa010_3 (.X1(fa101_1_s), .Y1(fa101_1_cout), .Cin(fa010_1_s), .Cout(fa010_3_cout), .S(fa010_3_s));
  FA101 fa101_2 (.X1(X3), .Y1(X4), .Cout(fa101_2_cout), .S(fa101_2_s));  // open: Cin
  FA101 fa101_3 (.X1(fa101_2_cout), .Y1(fa010_2_s), .Cin(fa010_2_cout), .Cout(fa101_3_cout), .S(fa101_3_s));
  FA101 fa101_4 (.X1(fa101_3_cout), .Y1(fa010_3_s), .Cin(fa010_3_cout), .Cout(fa101_4_cout), .S(fa101_4_s));
  FA111 fa111_1 (.X1(fa101_4_cout), .Y1(fa010_1_cout), .Cout(fa111_1_cout), .S(fa111_1_s));  // open: Cin
  FA010 fa010_4 (.X1(X0), .Y1(X1), .Cin(X2), .Cout(fa010_4_cout), .S(fa010_4_s));
  FA010 fa010_5 (.X1(fa010_4_s), .Y1(fa010_4_cout), .Cin(fa101_2_s), .Cout(fa010_5_cout), .S(fa010_5_s));
  FA010 fa010_6 (.X1(fa010_5_s), .Y1(fa010_5_cout), .Cin(fa101_3_s), .Cout(fa010_6_cout), .S(fa010_6_s));
  FA010 fa010_7 (.X1(fa010_6_s), .Y1(fa010_6_cout), .Cin(fa101_4_s), .Cout(fa010_7_cout), .S(fa010_7_s));
  FA010 fa010_8 (.X1(fa010_7_s), .Y1(fa010_7_cout), .Cin(fa111_1_s), .Cout(fa010_8_cout), .S(fa010_8_s));
  FA110 fa110_1 (.X1(fa010_8_s), .Y1(fa010_8_cout), .Cin(fa111_1_cout), .Cout(Cout), .S(S));
endmodule
