// Logisim project RCA.circ as structural Verilog: 6 circuits, main circuit main
module main (
  input  in_1,
  input  in_2,
  input  in_3,
  input  in_4,
  input  in_5,
  input  in_6,
  input  in_7,
  input  in_8,
  input  in_9,
  input  in_10,
  input  in_11,
  input  in_12,
  input  in_13,
  input  in_14,
  input  in_15,
  input  in_16,
  input  in_17,
  input  in_18,
  input  in_19,
  input  in_20,
  input  in_21,
  input  in_22,
  input  in_23,
  input  in_24,
  input  in_25,
  input  in_26,
  input  in_27,
  input  in_28,
  input  in_29,
  input  in_30,
  input  in_31,
  input  in_32,
  input  Uszkodzenie,
  input  Uszkodzenie_2,
  input  Uszkodzenie_3,
  input  Uszkodzenie_4,
  input  Uszkodzenie_5,
  input  Uszkodzenie_6,
  input  Uszkodzenie_7,
  input  Uszkodzenie_8,
  input  Uszkodzenie_9,
  input  Uszkodzenie_10,
  input  in_43,
  input  in_44,
  input  in_45,
  input  in_46,
  input  in_47,
  input  in_48,
  input  in_49,
  input  in_50,
  output out_51,
  output out_52,
  output out_53,
  output out_54,
  output out_55,
  output out_56,
  output out_57,
  output out_58,
  output out_59,
  output out_60,
  output out_61,
  output out_62,
  output out_63,
  output out_64,
  output out_65,
  output out_66,
  output out_67,
  output Uszkodzenie_11,
  output out_69,
  output out_70,
  output out_71,
  output out_72,
  output Uszkodzenie_12,
  output out_74,
  output out_75,
  output out_76,
  output out_77
);

  wire and_1_out, and_2_out, and_3_out, and_4_out, and_5_out, and_6_out, and_7_out, and_8_out, and_9_out,
       and_10_out, and_11_out, and_12_out, and_13_out, and_14_out, and_15_out, and_16_out, and_17_out,
       and_18_out, fa010_1_cout, fa010_1_s, fa010_2_cout, fa010_2_s, fa010_3_cout, fa010_3_s, fa010_4_cout,
       fa010_4_s, fa010_5_cout, fa010_5_s, fa010_6_cout, fa010_6_s, fa010_7_cout, fa010_7_s, fa010_8_cout,
       fa010_8_s, fa010_9_cout, fa010_9_s, fa010_10_cout, fa010_10_s, fa010_11_cout, fa010_11_s,
       fa010_12_cout, fa010_12_s, fa010_13_cout, fa010_13_s, fa010_14_cout, fa010_14_s, fa010_15_cout,
       fa010_15_s, fa010_16_cout, fa010_16_s, fa101_1_cout, fa101_1_s, fa101_2_cout, fa101_2_s, fa101_3_cout,
       fa101_3_s, fa101_4_cout, fa101_4_s, fa101_5_cout, fa101_5_s, fa101_6_cout, fa101_6_s, fa101_7_cout,
       fa101_7_s, fa101_8_cout, fa101_8_s, fa111_1_cout, fa111_1_s, fa111_2_cout, fa111_2_s, or_1_out,
       or_2_out, or_3_out, or_4_out, or_5_out, or_6_out, or_7_out, xor_2_out, xor_3_out, xor_4_out,
       xor_5_out, xor_6_out, xor_8_out, xor_9_out, xor_10_out, xor_11_out, xor_12_out, xor_13_out,
       xor_14_out, xor_16_out, xor_17_out, xor_18_out, xor_19_out, xor_20_out, xor_22_out, xor_23_out,
       xor_26_out, xor_27_out, xor_28_out, xor_29_out, xor_30_out, xor_32_out, xor_33_out, xor_34_out,
       xor_35_out, xor_36_out, xor_37_out, xor_38_out, xor_40_out, xor_41_out, xor_42_out, xor_43_out,
       xor_44_out, xor_46_out, xor_47_out;

  or or_1 (or_1_out, xor_2_out, xor_3_out);
  xor xor_1 (out_56, or_1_out, in_43);
  not not_1 (out_53, or_2_out);
  xor xor_2 (xor_2_out, in_17, and_1_out);
  xor xor_3 (xor_3_out, and_2_out, Uszkodzenie);
  and and_1 (and_1_out, in_9, in_13);
  and and_2 (and_2_out, xor_5_out, xor_8_out);
  or or_2 (or_2_out, and_3_out, and_4_out, and_5_out, and_6_out);
  xor xor_4 (xor_4_out, in_9, in_13);
  xor xor_5 (xor_5_out, xor_4_out, in_18);
  xor xor_6 (xor_6_out, xor_5_out, xor_8_out);
  xor xor_7 (out_57, xor_6_out, in_45);
  FA010 fa010_1 (.Cout(fa010_1_cout), .S(fa010_1_s));  // open: X1, Y1, Cin
  and and_3 (and_3_out, ~out_51, ~out_52, ~out_54, ~out_55);  // AND_Gate
  and and_4 (and_4_out, out_51, ~out_52, out_54, ~out_55);  // AND_Gate
  and and_5 (and_5_out, out_51, out_52, out_54, out_55);
  and and_6 (and_6_out, ~out_51, out_52, ~out_54, out_55);  // AND_Gate
  xor xor_8 (xor_8_out, or_3_out, Uszkodzenie_2);
  FA101 fa101_1 (.Cout(fa101_1_cout), .S(fa101_1_s));  // open: X1, Y1, Cin
  or or_3 (or_3_out, xor_10_out, xor_9_out);
  xor xor_9 (xor_9_out, and_8_out, Uszkodzenie_3);
  FA010 fa010_2 (.Cout(fa010_2_cout), .S(fa010_2_s));  // open: X1, Y1, Cin
  FA010 fa010_3 (.X1(fa101_1_s), .Y1(fa101_1_cout), .Cin(fa010_1_s), .Cout(fa010_3_cout), .S(fa010_3_s));
  and and_7 (and_7_out, in_10, in_14);
  xor xor_10 (xor_10_out, in_19, and_7_out);
  FA101 fa101_2 (.X1(out_57), .Y1(out_56), .Cout(fa101_2_cout), .S(fa101_2_s));  // open: Cin
  FA101 fa101_3 (.X1(fa101_2_cout), .Y1(fa010_2_s), .Cin(fa010_2_cout), .Cout(fa101_3_cout), .S(fa101_3_s));
  FA101 fa101_4 (.X1(fa101_3_cout), .Y1(fa010_3_s), .Cin(fa010_3_cout), .Cout(fa101_4_cout), .S(fa101_4_s));
  FA111 fa111_1 (.X1(fa101_4_cout), .Y1(fa010_1_cout), .Cout(fa111_1_cout), .S(fa111_1_s));  // open: Cin
  xor xor_11 (xor_11_out, in_10, in_14);
  and and_8 (and_8_out, xor_12_out, xor_13_out);
  xor xor_12 (xor_12_out, xor_11_out, in_20);
  xor xor_13 (xor_13_out, or_4_out, Uszkodzenie_4);
  xor xor_14 (xor_14_out, xor_12_out, xor_13_out);
  xor xor_15 (out_58, xor_14_out, in_46);
  FA010 fa010_4 (.X1(out_60), .Y1(out_59), .Cin(out_58), .Cout(fa010_4_cout), .S(fa010_4_s));
  FA010 fa010_5 (.X1(fa010_4_s), .Y1(fa010_4_cout), .Cin(fa101_2_s), .Cout(fa010_5_cout), .S(fa010_5_s));
  FA010 fa010_6 (.X1(fa010_5_s), .Y1(fa010_5_cout), .Cin(fa101_3_s), .Cout(fa010_6_cout), .S(fa010_6_s));
  FA010 fa010_7 (.X1(fa010_6_s), .Y1(fa010_6_cout), .Cin(fa101_4_s), .Cout(fa010_7_cout), .S(fa010_7_s));
  FA010 fa010_8 (.X1(fa010_7_s), .Y1(fa010_7_cout), .Cin(fa111_1_s), .Cout(fa010_8_cout), .S(fa010_8_s));
  FA110 fa110_1 (.X1(fa010_8_s), .Y1(fa010_8_cout), .Cin(fa111_1_cout), .Cout(out_51), .S(out_52));
  or or_4 (or_4_out, xor_17_out, xor_16_out);
  xor xor_16 (xor_16_out, and_10_out, Uszkodzenie_5);
  and and_9 (and_9_out, in_11, in_15);
  xor xor_17 (xor_17_out, in_21, and_9_out);
  and and_10 (and_10_out, xor_19_out, xor_22_out);
  xor xor_18 (xor_18_out, in_11, in_15);
  xor xor_19 (xor_19_out, xor_18_out, in_22);
  xor xor_20 (xor_20_out, xor_19_out, xor_22_out);
  xor xor_21 (out_59, xor_20_out, in_47);
  xor xor_22 (xor_22_out, in_23, and_11_out);
  and and_11 (and_11_out, in_12, in_16);
  xor xor_23 (xor_23_out, in_12, in_16);
  xor xor_24 (out_60, xor_23_out, in_24);
  or or_5 (or_5_out, xor_27_out, xor_26_out);
  xor xor_25 (out_61, or_5_out, in_44);
  xor xor_26 (xor_26_out, and_13_out, Uszkodzenie_6);
  and and_12 (and_12_out, in_1, in_5);
  xor xor_27 (xor_27_out, in_25, and_12_out);
  and and_13 (and_13_out, xor_29_out, xor_32_out);
  xor xor_28 (xor_28_out, in_1, in_5);
  xor xor_29 (xor_29_out, xor_28_out, in_26);
  xor xor_30 (xor_30_out, xor_29_out, xor_32_out);
  xor xor_31 (out_62, xor_30_out, in_48);
  FA010 fa010_9 (.Cout(fa010_9_cout), .S(fa010_9_s));  // open: X1, Y1, Cin
  xor xor_32 (xor_32_out, or_6_out, Uszkodzenie_7);
  FA101 fa101_5 (.Cout(fa101_5_cout), .S(fa101_5_s));  // open: X1, Y1, Cin
  or or_6 (or_6_out, xor_34_out, xor_33_out);
  xor xor_33 (xor_33_out, and_15_out, Uszkodzenie_8);
  FA010 fa010_10 (.Cout(fa010_10_cout), .S(fa010_10_s));  // open: X1, Y1, Cin
  FA010 fa010_11 (.X1(fa101_5_s), .Y1(fa101_5_cout), .Cin(fa010_9_s), .Cout(fa010_11_cout), .S(fa010_11_s));
  and and_14 (and_14_out, in_2, in_6);
  xor xor_34 (xor_34_out, in_27, and_14_out);
  and and_15 (and_15_out, xor_36_out, xor_38_out);
  FA101 fa101_6 (.X1(out_62), .Y1(out_61), .Cout(fa101_6_cout), .S(fa101_6_s));  // open: Cin
  FA101 fa101_7 (.X1(fa101_6_cout), .Y1(fa010_10_s), .Cin(fa010_10_cout), .Cout(fa101_7_cout), .S(fa101_7_s));
  FA101 fa101_8 (.X1(fa101_7_cout), .Y1(fa010_11_s), .Cin(fa010_11_cout), .Cout(fa101_8_cout), .S(fa101_8_s));
  FA111 fa111_2 (.X1(fa101_8_cout), .Y1(fa010_9_cout), .Cout(fa111_2_cout), .S(fa111_2_s));  // open: Cin
  xor xor_35 (xor_35_out, in_2, in_6);
  xor xor_36 (xor_36_out, xor_35_out, in_28);
  xor xor_37 (xor_37_out, xor_36_out, xor_38_out);
  xor xor_38 (xor_38_out, or_7_out, Uszkodzenie_9);
  xor xor_39 (out_63, xor_37_out, in_49);
  FA010 fa010_12 (.X1(out_65), .Y1(out_64), .Cin(out_63), .Cout(fa010_12_cout), .S(fa010_12_s));
  FA010 fa010_13 (.X1(fa010_12_s), .Y1(fa010_12_cout), .Cin(fa101_6_s), .Cout(fa010_13_cout), .S(fa010_13_s));
  FA010 fa010_14 (.X1(fa010_13_s), .Y1(fa010_13_cout), .Cin(fa101_7_s), .Cout(fa010_14_cout), .S(fa010_14_s));
  FA010 fa010_15 (.X1(fa010_14_s), .Y1(fa010_14_cout), .Cin(fa101_8_s), .Cout(fa010_15_cout), .S(fa010_15_s));
  FA010 fa010_16 (.X1(fa010_15_s), .Y1(fa010_15_cout), .Cin(fa111_2_s), .Cout(fa010_16_cout), .S(fa010_16_s));
  FA110 fa110_2 (.X1(fa010_16_s), .Y1(fa010_16_cout), .Cin(fa111_2_cout), .Cout(out_54), .S(out_55));
  or or_7 (or_7_out, xor_40_out, xor_41_out);
  xor xor_40 (xor_40_out, in_29, and_16_out);
  xor xor_41 (xor_41_out, and_17_out, Uszkodzenie_10);
  and and_16 (and_16_out, in_3, in_7);
  and and_17 (and_17_out, xor_43_out, xor_46_out);
  xor xor_42 (xor_42_out, in_3, in_7);
  xor xor_43 (xor_43_out, xor_42_out, in_30);
  xor xor_44 (xor_44_out, xor_43_out, xor_46_out);
  xor xor_45 (out_64, xor_44_out, in_50);
  and and_18 (and_18_out, in_4, in_8);
  xor xor_46 (xor_46_out, in_31, and_18_out);
  xor xor_47 (xor_47_out, in_4, in_8);
  xor xor_48 (out_65, xor_47_out, in_32);

  assign out_66 = out_54;
  assign out_67 = out_55;
  assign out_69 = out_57;
  assign out_70 = out_58;
  assign out_71 = out_59;
  assign out_72 = out_60;
  assign out_74 = out_62;
  assign out_75 = out_63;
  assign out_76 = out_64;
  assign out_77 = out_65;
  assign Uszkodzenie_11 = out_56;
  assign Uszkodzenie_12 = out_61;

  // Notes on the sheet:
  //   Jednostka kontrolna
  //   Uszkodzenie
  //   Uszkodzenie
  //   Uszkodzenie
  //   x2
  //   x1
  //   y2
  //   y1
  //   Uszkodzenie
  //   Uszkodzenie
  //   Uszkodzenie
  //   Uszkodzenie
  //   Uszkodzenie
  //   Uszkodzenie
  //   Uszkodzenie
  //   Uszkodzenie
  //   Uszkodzenie
  //   Uszkodzenie
  //   Uszkodzenie
  //   Uszkodzenie
  //   Uszkodzenie
  //   Uszkodzenie
  //   Uszkodzenie
  //   Uszkodzenie
  //   Uszkodzenie
  //   Uszkodzenie
  //   Uszkodzenie
endmodule

module FA101 (
  input  X1,
  input  Y1,
  input  Cin,
  output Cout,
  output S
);

  wire and_1_out, and_2_out, not_1_out, not_2_out, xor_1_out;

  or or_1 (Cout, and_1_out, and_2_out);
  not not_1 (not_1_out, X1);
  and and_1 (and_1_out, not_1_out, Y1);
  and and_2 (and_2_out, xor_1_out, not_2_out);
  xor xor_1 (xor_1_out, not_1_out, Y1);
  xor xor_2 (S, xor_1_out, not_2_out);
  not not_2 (not_2_out, Cin);
endmodule

module FA010 (
  input  X1,
  input  Y1,
  input  Cin,
  output Cout,
  output S
);

  wire and_1_out, and_2_out, not_1_out, xor_1_out;

  or or_1 (Cout, and_1_out, and_2_out);
  and and_1 (and_1_out, X1, not_1_out);
  and and_2 (and_2_out, xor_1_out, Cin);
  not not_1 (not_1_out, Y1);
  xor xor_1 (xor_1_out, X1, not_1_out);
  xor xor_2 (S, xor_1_out, Cin);
endmodule

module FA111 (
  input  X1,
  input  Y1,
  input  Cin,
  output Cout,
  output S
);

  wire and_1_out, and_2_out, not_1_out, not_2_out, not_3_out, xor_1_out;

  or or_1 (Cout, and_1_out, and_2_out);
  not not_1 (not_1_out, X1);
  and and_1 (and_1_out, not_1_out, not_2_out);
  and and_2 (and_2_out, xor_1_out, not_3_out);
  xor xor_1 (xor_1_out, not_1_out, not_2_out);
  xor xor_2 (S, xor_1_out, not_3_out);
  not not_2 (not_2_out, Y1);
  not not_3 (not_3_out, Cin);
endmodule

module FA110 (
  input  X1,
  input  Y1,
  input  Cin,
  output Cout,
  output S
);

  wire and_1_out, and_2_out, not_1_out, not_2_out, xor_1_out;

  or or_1 (Cout, and_1_out, and_2_out);
  and and_1 (and_1_out, X1, not_1_out);
  and and_2 (and_2_out, xor_1_out, not_2_out);
  xor xor_1 (xor_1_out, X1, not_1_out);
  xor xor_2 (S, xor_1_out, not_2_out);
  not not_1 (not_1_out, Y1);
  not not_2 (not_2_out, Cin);
endmodule

module sumatorMOD3 (
  input  in_1,
  input  in_2,
  input  in_3,
  input  in_4,
  output out_5,
  output out_6
);

  wire fa010_1_cout, fa010_1_s;

  FA010 fa010_1 (.X1(in_4), .Y1(in_3), .Cin(in_2), .Cout(fa010_1_cout), .S(fa010_1_s));
  FA110 fa110_1 (.X1(fa010_1_s), .Y1(fa010_1_cout), .Cin(in_1), .Cout(out_5), .S(out_6));
endmodule
