// Logisim project ughhhh_cla_adder.circ as structural Verilog: 2 circuits, main circuit main
module main (
  input  in_1,
  input  in_2,
  input  in_3,
  input  in_4,
  input  in_5,
  input  in_6,
  input  in_7,
  input  in_8,
  input  in_9,
  output out_10,
  output out_11,
  output out_12,
  output out_13,
  output out_14
);

  wire and_1_out, and_2_out, and_3_out, and_4_out, and_5_out, and_6_out, and_7_out, and_8_out, and_9_out,
       and_10_out, and_11_out, and_12_out, and_13_out, and_14_out, or_1_out, or_2_out, or_3_out, or_4_out,
       or_5_out, or_6_out, or_7_out, or_8_out, xor_1_out, xor_2_out, xor_3_out, xor_4_out, xor_5_out,
       xor_6_out, xor_7_out, xor_8_out, xor_9_out, xor_10_out, xor_11_out, xor_12_out, xor_14_out,
       xor_15_out, xor_16_out, xor_17_out, xor_18_out, xor_19_out, xor_20_out, xor_21_out;

  and and_1 (and_1_out, in_2, in_6);
  buf xor_1 (xor_1_out, and_1_out);  // XOR_Gate
  or or_1 (or_1_out, in_2, in_6);
  buf xor_2 (xor_2_out, or_1_out);  // XOR_Gate
  and and_2 (and_2_out, in_1, xor_2_out);
  and and_3 (and_3_out, in_3, in_7);
  buf xor_3 (xor_3_out, and_3_out);  // XOR_Gate
  buf xor_4 (xor_4_out, and_2_out);  // XOR_Gate
  or or_2 (or_2_out, xor_1_out, xor_4_out);
  buf xor_5 (xor_5_out, or_2_out);  // XOR_Gate
  or or_3 (or_3_out, in_3, in_7);
  buf xor_6 (xor_6_out, or_3_out);  // XOR_Gate
  and and_4 (and_4_out, in_1, xor_2_out, xor_6_out);
  and and_5 (and_5_out, xor_6_out, xor_1_out);
  and and_6 (and_6_out, in_4, in_8);
  buf xor_7 (xor_7_out, and_6_out);  // XOR_Gate
  or or_4 (or_4_out, and_5_out, xor_3_out, and_4_out);
  buf xor_8 (xor_8_out, or_4_out);  // XOR_Gate
  or or_5 (or_5_out, in_4, in_8);
  buf xor_9 (xor_9_out, or_5_out);  // XOR_Gate
  and and_7 (and_7_out, in_1, xor_2_out, xor_6_out, xor_9_out);
  and and_8 (and_8_out, xor_9_out, xor_6_out, xor_1_out);
  and and_9 (and_9_out, xor_9_out, xor_3_out);
  and and_10 (and_10_out, in_5, in_9);
  buf xor_10 (xor_10_out, and_10_out);  // XOR_Gate
  or or_6 (or_6_out, and_9_out, and_8_out, xor_7_out, and_7_out);
  buf xor_11 (xor_11_out, or_6_out);  // XOR_Gate
  or or_7 (or_7_out, in_5, in_9);
  buf xor_12 (xor_12_out, or_7_out);  // XOR_Gate
  and and_11 (and_11_out, in_1, xor_2_out, xor_6_out, xor_9_out, xor_12_out);
  and and_12 (and_12_out, xor_12_out, xor_6_out, xor_9_out, xor_1_out);
  and and_13 (and_13_out, xor_12_out, xor_9_out, xor_3_out);
  and and_14 (and_14_out, xor_12_out, xor_7_out);
  or or_8 (or_8_out, and_14_out, and_13_out, and_12_out, xor_10_out, and_11_out);
  buf xor_13 (out_14, or_8_out);  // XOR_Gate
  xor xor_14 (xor_14_out, in_2, in_6);
  xor xor_15 (xor_15_out, in_3, in_7);
  xor xor_16 (xor_16_out, in_4, in_8);
  xor xor_17 (xor_17_out, in_5, in_9);
  xor xor_18 (xor_18_out, xor_14_out, in_1);
  xor xor_19 (xor_19_out, xor_15_out, xor_5_out);
  xor xor_20 (xor_20_out, xor_16_out, xor_8_out);
  xor xor_21 (xor_21_out, xor_17_out, xor_11_out);
  buf xor_22 (out_10, xor_18_out);  // XOR_Gate
  buf xor_23 (out_11, xor_19_out);  // XOR_Gate
  buf xor_24 (out_12, xor_20_out);  // XOR_Gate
  buf xor_25 (out_13, xor_21_out);  // XOR_Gate
endmodule

module mod3 (
  input  in_1,
  input  in_2,
  input  in_3,
  input  in_4,
  input  in_5,
  output out_6,
  output out_7,
  output out_8
);

  wire and_1_out, and_2_out, and_3_out, and_4_out, and_5_out, or_1_out, or_2_out, or_3_out, or_4_out,
       xor_1_out, xor_2_out, xor_3_out, xor_4_out, xor_5_out, xor_6_out, xor_8_out, xor_9_out, xor_10_out,
       xor_11_out;

  and and_1 (and_1_out, in_2, in_4);
  buf xor_1 (xor_1_out, and_1_out);  // XOR_Gate
  or or_1 (or_1_out, in_2, in_4);
  buf xor_2 (xor_2_out, or_1_out);  // XOR_Gate
  and and_2 (and_2_out, in_1, xor_2_out);
  and and_3 (and_3_out, in_3, in_5);
  buf xor_3 (xor_3_out, and_3_out);  // XOR_Gate
  buf xor_4 (xor_4_out, and_2_out);  // XOR_Gate
  or or_2 (or_2_out, xor_1_out, xor_4_out);
  buf xor_5 (xor_5_out, or_2_out);  // XOR_Gate
  or or_3 (or_3_out, in_3, in_5);
  buf xor_6 (xor_6_out, or_3_out);  // XOR_Gate
  and and_4 (and_4_out, in_1, xor_2_out, xor_6_out);
  and and_5 (and_5_out, xor_6_out, xor_1_out);
  or or_4 (or_4_out, and_5_out, xor_3_out, and_4_out);
  buf xor_7 (out_8, or_4_out);  // XOR_Gate
  xor xor_8 (xor_8_out, in_2, in_4);
  xor xor_9 (xor_9_out, in_3, in_5);
  xor xor_10 (xor_10_out, xor_8_out, in_1);
  xor xor_11 (xor_11_out, xor_9_out, xor_5_out);
  buf xor_12 (out_6, xor_10_out);  // XOR_Gate
  buf xor_13 (out_7, xor_11_out);  // XOR_Gate
endmodule
